# Fritzing sketch gun_test (saved by Fritzing 0.9.3b)
breadboards: 1

parts:
  Part1 = Logic Level Converter
  Raspberry_Pi_Zero1 = Raspberry Pi Zero
  M1 = DC Motor  # not connected
  Power_plug1 = Power plug
  U1 = mystery part, 3 pins [chip_label=TSOP4838]  # not connected
  U2 = mystery part, 3 pins [chip_label=TSOP4838]
  Q1 = MOSFET-NCHANNEL [part_number=bs170 package=to-92]
  R1 = Resistor [tolerance=±5% resistance=100k package="0402 [SMD]"]
  LED1 = LED - 5mm [color="Infrared (940nm)" package="5 mm [THT]"]
  PL1 = PL9823 (WS2812 clone) [package="5 mm [THT]"]
  PL2 = PL9823 (WS2812 clone) [package="5 mm [THT]"]

nets:
  N1: Part1.TX2_LV, Raspberry_Pi_Zero1.GIPO18
  GND: Part1.GND, Raspberry_Pi_Zero1.GND, Power_plug1.GND, U2.pin2, Q1.G, R1.Pin_1, PL1.GND, PL2.GND
  3V3: Part1.LV, Raspberry_Pi_Zero1.3v3, Raspberry_Pi_Zero1.3V3
  N2: Part1.RX_LV, Raspberry_Pi_Zero1.GIPO22
  N3: Part1.TX_LV, Raspberry_Pi_Zero1.GIPO23
  N4: Part1.TX_HV, U2.pin1
  N5: Part1.RX_HV, Q1.S, R1.Pin_0
  VDD: Part1.HV, Power_plug1.VCC, U2.pin3, LED1.anode, PL1.VDD, PL2.VDD
  N6: Part1.TX2_HV, PL1.DIN
  N7: Q1.D, LED1.cathode
  N8: PL1.DO, PL2.DIN

custom parts:
  PL9823 (WS2812 clone): A Ws2812 compatible LED PL9823
